// Logisim project 8BitBenEater.circ as structural Verilog: 13 circuits, main circuit main
module main (
  input  in_1,
  input  in_2,
  input  PROGRAM_MODE
);

  wire A_IN, A_OUT, alu_1_cout, ALU_OUT, B_IN, bcd_to_7_segment_decoder_3_p1, binary_to_bcd_converter_1_p2,
       binary_to_bcd_converter_1_p4, button_1_out, clk_1_clk_out, clock_1_out, COUNTER_ENB, COUNTER_OUT,
       COUT, decoder_1_out0, decoder_1_out1, decoder_1_out2, decoder_1_out3, decoder_1_out4, decoder_1_out5,
       FLAGS_IN, HALT, INR_IN, INR_OUT, JUMP, MAR_IN, multiplexer_3_out, not_1_out, not_2_out, or_1_out,
       OUTPUT_REG_IN, RAM_IN, RAM_OUT, RESET_out, SUB, ZERO, zero_flag_1_zero;
  wire [3:0] dipswitch_1_sw4, mar_1_always_out, multiplexer_1_out, step_counter_1_binary_out;
  wire [7:0] alu_1_always_out, binary_to_bcd_converter_1_p1, dipswitch_2_sw8,
       instruction_register_1_always_out, mar_1_data_out, memory_1_always_out, multiplexer_2_out,
       register_a_1_always_out, register_b_1_always_out;
  wire [10:10] pull_resistor_1_node;

  Button RESET (.out(RESET_out));
  DipSwitch #(.number(4)) dipswitch_1 (
    .sw1(dipswitch_1_sw4[3]), .sw2(dipswitch_1_sw4[2]), .sw3(dipswitch_1_sw4[1]), .sw4(dipswitch_1_sw4[0]));
  DipSwitch dipswitch_2 (
    .sw1(dipswitch_2_sw8[7]), .sw2(dipswitch_2_sw8[6]), .sw3(dipswitch_2_sw8[5]), .sw4(dipswitch_2_sw8[4]),
    .sw5(dipswitch_2_sw8[3]), .sw6(dipswitch_2_sw8[2]), .sw7(dipswitch_2_sw8[1]), .sw8(dipswitch_2_sw8[0]));
  Button button_1 (.out(button_1_out));
  not not_1 (not_1_out, clk_1_clk_out);
  or or_1 (or_1_out, RESET_out, decoder_1_out5);
  LED led_1 (.in(not_2_out));
  LED led_2 (.in(PROGRAM_MODE));
  not not_2 (not_2_out, PROGRAM_MODE);
  Clock clock_1 (.out(clock_1_out));
  Multiplexer #(.width(4)) multiplexer_1 (
    .in0(mar_1_always_out), .in1(dipswitch_1_sw4), .out(multiplexer_1_out), .sel(PROGRAM_MODE));
  Multiplexer #(.width(8)) multiplexer_2 (
    .in0(mar_1_data_out), .in1(dipswitch_2_sw8), .out(multiplexer_2_out), .sel(PROGRAM_MODE));
  Multiplexer multiplexer_3 (.in0(RAM_IN), .in1(button_1_out), .out(multiplexer_3_out), .sel(PROGRAM_MODE));
  LED led_3 (.in(instruction_register_1_always_out[7]));
  STEP_COUNTER step_counter_1 (.CLOCK(not_1_out), .RESET(or_1_out), .BINARY_OUT(step_counter_1_binary_out));
  MAR mar_1 (
    .MAR_IN(MAR_IN), .CLOCK(clk_1_clk_out), .MAR_RESET(RESET_out), .DATA_IN(mar_1_data_out[3:0]),
    .ALWAYS_OUT(mar_1_always_out), .DATA_OUT(mar_1_data_out[3:0]));  // open: MAR_OUT
  LED led_4 (.in(multiplexer_1_out[3]));
  LED led_5 (.in(memory_1_always_out[7]));
  LED led_6 (.in(memory_1_always_out[6]));
  INSTRUCTION_REGISTER instruction_register_1 (
    .DATA_IN(mar_1_data_out), .STORE(INR_IN), .DATA_OUT_ENABLE(INR_OUT), .RESET(RESET_out),
    .CLOCK(clk_1_clk_out), .ALWAYS_OUT(instruction_register_1_always_out), .DATA_OUT(mar_1_data_out));
  LED led_7 (.in(instruction_register_1_always_out[6]));
  LED led_8 (.in(instruction_register_1_always_out[5]));
  LED led_9 (.in(instruction_register_1_always_out[4]));
  LED led_10 (.in(instruction_register_1_always_out[3]));
  LED led_11 (.in(multiplexer_1_out[2]));
  LED led_12 (.in(multiplexer_1_out[1]));
  LED led_13 (.in(multiplexer_1_out[0]));
  MEMORY memory_1 (
    .RAM_OUT_ENB(RAM_OUT), .STORE(multiplexer_3_out), .CLOCK(clk_1_clk_out), .ADDRESS(multiplexer_1_out),
    .DATA(multiplexer_2_out), .ALWAYS_OUT(memory_1_always_out), .RAM_OUT(mar_1_data_out));
  LED led_14 (.in(memory_1_always_out[5]));
  LED led_15 (.in(memory_1_always_out[4]));
  LED led_16 (.in(memory_1_always_out[3]));
  LED led_17 (.in(memory_1_always_out[2]));
  LED led_18 (.in(instruction_register_1_always_out[2]));
  LED led_19 (.in(instruction_register_1_always_out[1]));
  LED led_20 (.in(instruction_register_1_always_out[0]));
  LED led_21 (.in(decoder_1_out0));
  LED led_22 (.in(decoder_1_out1));
  LED led_23 (.in(decoder_1_out2));
  LED led_24 (.in(decoder_1_out3));
  Decoder #(.select(3)) decoder_1 (
    .out0(decoder_1_out0), .out1(decoder_1_out1), .out2(decoder_1_out2), .out3(decoder_1_out3),
    .out4(decoder_1_out4), .out5(decoder_1_out5), .sel(step_counter_1_binary_out[2:0]));  // open: out6, out7, en
  CLK clk_1 (.CLK_IN(clock_1_out), .CLK_ENB(in_1), .CLK_MANUAL(in_2), .HALT(HALT), .CLK_OUT(clk_1_clk_out));
  LED led_25 (.in(memory_1_always_out[1]));
  LED led_26 (.in(memory_1_always_out[0]));
  Pull_Resistor pull_resistor_1 (.node(pull_resistor_1_node[10]));
  LED led_27 (.in(decoder_1_out4));
  ROM #(.addrWidth(11)) rom_1 (
    .addr({{2{pull_resistor_1_node[10]}}, ZERO, COUT, instruction_register_1_always_out[7:4], step_counter_1_binary_out[2:0]}),
    .data({HALT, MAR_IN, RAM_IN, RAM_OUT, INR_OUT, INR_IN, A_IN, A_OUT}));
  ROM #(.addrWidth(11)) rom_2 (
    .addr({{2{pull_resistor_1_node[10]}}, ZERO, COUT, instruction_register_1_always_out[7:4], step_counter_1_binary_out[2:0]}),
    .data({ALU_OUT, SUB, B_IN, OUTPUT_REG_IN, COUNTER_ENB, COUNTER_OUT, JUMP, FLAGS_IN}));
  LED led_28 (.in(mar_1_data_out[7]));
  LED led_29 (.in(mar_1_data_out[6]));
  Pull_Resistor pull_resistor_2 (.node(mar_1_data_out[7]));
  Pull_Resistor pull_resistor_3 (.node(mar_1_data_out[6]));
  LED led_30 (.in(mar_1_data_out[5]));
  LED led_31 (.in(mar_1_data_out[4]));
  LED led_32 (.in(mar_1_data_out[3]));
  LED led_33 (.in(mar_1_data_out[2]));
  Pull_Resistor pull_resistor_4 (.node(mar_1_data_out[5]));
  Pull_Resistor pull_resistor_5 (.node(mar_1_data_out[4]));
  Pull_Resistor pull_resistor_6 (.node(mar_1_data_out[3]));
  Pull_Resistor pull_resistor_7 (.node(mar_1_data_out[2]));
  LED led_34 (.in(mar_1_data_out[1]));
  LED led_35 (.in(mar_1_data_out[0]));
  Pull_Resistor pull_resistor_8 (.node(mar_1_data_out[1]));
  Pull_Resistor pull_resistor_9 (.node(mar_1_data_out[0]));
  PROGRAM_COUNTER program_counter_1 (
    .RESET(RESET_out), .JUMP(JUMP), .COUNTER_ENABLE(COUNTER_ENB), .CLOCK(clk_1_clk_out),
    .ADDRESS_IN(mar_1_data_out[3:0]), .COUNTER_OUT(COUNTER_OUT), .ADDRESS_OUT(mar_1_data_out[3:0]));  // open: ALWAYS_OUT
  _7_Segment_Display u_7_segment_display_1 ();  // open: g, f, a, b, e, d, c, dp
  // BCD_to_7_Segment_decoder bcd_to_7_segment_decoder_1: pin names not known
  // Binary_to_BCD_converter #(.binvalue(8)) binary_to_bcd_converter_1: pin names not known; wires that end beside it: binary_to_bcd_converter_1_p1, binary_to_bcd_converter_1_p2, binary_to_bcd_converter_1_p2, binary_to_bcd_converter_1_p4
  LED led_36 (.in(HALT));
  LED led_37 (.in(MAR_IN));
  LED led_38 (.in(RAM_IN));
  LED led_39 (.in(RAM_OUT));
  REGISTER_A register_a_1 (
    .DATA_IN(mar_1_data_out), .A_IN(A_IN), .A_OUT(A_OUT), .CLOCK(clk_1_clk_out), .A_RESET(RESET_out),
    .ALWAYS_OUT(register_a_1_always_out), .DATA_OUT(mar_1_data_out));
  ALU alu_1 (
    .A_IN(register_a_1_always_out), .B_IN(register_b_1_always_out), .OUTPUT_ENB(ALU_OUT), .SUB(SUB),
    .ALWAYS_OUT(alu_1_always_out), .ALU_DATA_OUT(mar_1_data_out), .COUT(alu_1_cout));
  REGISTER_B register_b_1 (
    .B_IN(B_IN), .CLOCK(clk_1_clk_out), .RESET(RESET_out), .DATA_IN(mar_1_data_out),
    .ALWAYS_OUT(register_b_1_always_out));  // open: B_OUT, DATA_OUT
  _7_Segment_Display u_7_segment_display_2 ();  // open: g, f, a, b, e, d, c, dp
  _7_Segment_Display u_7_segment_display_3 ();  // open: g, f, a, b, e, d, c, dp
  // BCD_to_7_Segment_decoder bcd_to_7_segment_decoder_2: pin names not known; wires that end beside it: binary_to_bcd_converter_1_p4
  // BCD_to_7_Segment_decoder bcd_to_7_segment_decoder_3: pin names not known; wires that end beside it: bcd_to_7_segment_decoder_3_p1, bcd_to_7_segment_decoder_3_p1
  OUTPUT_REGISTER output_register_1 (
    .STORE(OUTPUT_REG_IN), .CLOCK(clk_1_clk_out), .RESET(RESET_out), .DATA_IN(mar_1_data_out),
    .DATA_OUT(binary_to_bcd_converter_1_p1));
  LED led_40 (.in(INR_OUT));
  LED led_41 (.in(INR_IN));
  LED led_42 (.in(A_IN));
  LED led_43 (.in(A_OUT));
  LED led_44 (.in(ALU_OUT));
  LED led_45 (.in(SUB));
  LED led_46 (.in(B_IN));
  LED led_47 (.in(OUTPUT_REG_IN));
  ZERO_FLAG zero_flag_1 (.in_1(alu_1_always_out), .ZERO(zero_flag_1_zero));
  LED led_48 (.in(COUNTER_ENB));
  LED led_49 (.in(COUNTER_OUT));
  LED led_50 (.in(JUMP));
  LED led_51 (.in(FLAGS_IN));
  FLAGS flags_1 (
    .CARRY(alu_1_cout), .ZERO(zero_flag_1_zero), .STORE(FLAGS_IN), .CLOCK(clk_1_clk_out), .CARRY_OUT(ZERO),
    .ZERO_OUT(COUT));  // open: RESET
  LED led_52 (.in(ZERO));
  LED led_53 (.in(COUT));

  // Notes on the sheet:
  //   contents of rom_1 (hex, n*v repeats v):
  //   40 14 6*0 40 14 48 12 4*0 40 14 48 10 2 0 0 0 40 14 48 10 2 0 0 0 40 14 48 21 4*0 40 14 a 5*0 40 14
  //   8 5*0 40 14 6*0 40 14 6*0 40 14 6*0 40 14 6*0 40 14 6*0 40 14 6*0 40 14 6*0 40 14 1 5*0 40 14 80 5*0
  //   40 14 6*0 40 14 48 12 4*0 40 14 48 10 2 0 0 0 40 14 48 10 2 0 0 0 40 14 48 21 4*0 40 14 a 5*0 40 14
  //   8 5*0 40 14 8 5*0 40 14 6*0 40 14 6*0 40 14 6*0 40 14 6*0 40 14 6*0 40 14 6*0 40 14 1 5*0 40 14 80
  //   5*0 40 14 6*0 40 14 48 12 4*0 40 14 48 10 2 0 0 0 40 14 48 10 2 0 0 0 40 14 48 21 4*0 40 14 a 5*0 40
  //   14 8 5*0 40 14 6*0 40 14 8 5*0 40 14 6*0 40 14 6*0 40 14 6*0 40 14 6*0 40 14 6*0 40 14 1 5*0 40 14
  //   80 5*0 40 14 6*0 40 14 48 12 4*0 40 14 48 10 2 0 0 0 40 14 48 10 2 0 0 0 40 14 48 21 4*0 40 14 a 5*0
  //   40 14 8 5*0 40 14 8 5*0 40 14 8 5*0 40 14 6*0 40 14 6*0 40 14 6*0 40 14 6*0 40 14 6*0 40 14 1 5*0 40
  //   14 80
  //   contents of rom_2 (hex, n*v repeats v):
  //   4 8 6*0 4 8 6*0 4 8 0 20 81 0 0 0 4 8 0 20 c1 0 0 0 4 8 6*0 4 8 6*0 4 8 2 5*0 4 8 6*0 4 8 6*0 4 8
  //   6*0 4 8 6*0 4 8 6*0 4 8 6*0 4 8 6*0 4 8 10 5*0 4 8 6*0 4 8 6*0 4 8 6*0 4 8 0 20 81 0 0 0 4 8 0 20 c1
  //   0 0 0 4 8 6*0 4 8 6*0 4 8 2 5*0 4 8 2 5*0 4 8 6*0 4 8 6*0 4 8 6*0 4 8 6*0 4 8 6*0 4 8 6*0 4 8 10 5*0
  //   4 8 6*0 4 8 6*0 4 8 6*0 4 8 0 20 81 0 0 0 4 8 0 20 c1 0 0 0 4 8 6*0 4 8 6*0 4 8 2 5*0 4 8 6*0 4 8 2
  //   5*0 4 8 6*0 4 8 6*0 4 8 6*0 4 8 6*0 4 8 6*0 4 8 10 5*0 4 8 6*0 4 8 6*0 4 8 6*0 4 8 0 20 81 0 0 0 4 8
  //   0 20 c1 0 0 0 4 8 6*0 4 8 6*0 4 8 2 5*0 4 8 2 5*0 4 8 2 5*0 4 8 6*0 4 8 6*0 4 8 6*0 4 8 6*0 4 8 6*0
  //   4 8 10 5*0 4 8
endmodule

module CLK (
  input  CLK_IN,
  input  CLK_ENB,
  input  CLK_MANUAL,
  input  HALT,
  output CLK_OUT
);

  wire and_1_out, and_2_out, not_1_out, not_2_out, or_1_out;

  not not_1 (not_1_out, CLK_ENB);
  not not_2 (not_2_out, HALT);
  and and_1 (and_1_out, CLK_IN, CLK_ENB);
  and and_2 (and_2_out, not_1_out, CLK_MANUAL);
  or or_1 (or_1_out, and_1_out, and_2_out);
  and and_3 (CLK_OUT, or_1_out, not_2_out);
endmodule

module PROGRAM_COUNTER (
  input  RESET,
  input  JUMP,
  input  COUNTER_ENABLE,
  input  CLOCK,
  input  [3:0] ADDRESS_IN,
  input  COUNTER_OUT,
  output [3:0] ALWAYS_OUT,
  output [3:0] ADDRESS_OUT
);

  Counter #(.max('hf), .width(4)) counter_1 (
    .clr(RESET), .load(JUMP), .up(COUNTER_ENABLE), .count(COUNTER_ENABLE), .clk(CLOCK), .D(ADDRESS_IN),
    .Q(ALWAYS_OUT));  // open: carry
  assign ADDRESS_OUT = COUNTER_OUT ? ALWAYS_OUT : 4'bz;  // Controlled_Buffer controlled_buffer_1
endmodule

module REGISTER_A (
  input  [7:0] DATA_IN,
  input  A_IN,
  input  A_OUT,
  input  CLOCK,
  input  A_RESET,
  output [7:0] ALWAYS_OUT,
  output [7:0] DATA_OUT
);

  Register register_1 (.D(DATA_IN), .en(A_IN), .clk(CLOCK), .Q(ALWAYS_OUT), .clr(A_RESET));
  assign DATA_OUT = A_OUT ? ALWAYS_OUT : 8'bz;  // Controlled_Buffer controlled_buffer_1
endmodule

module ALU (
  input  [7:0] A_IN,
  input  [7:0] B_IN,
  input  OUTPUT_ENB,
  input  SUB,
  output [7:0] ALWAYS_OUT,
  output [7:0] ALU_DATA_OUT,
  output COUT
);

  wire not_1_out;
  wire [7:0] controlled_buffer_1_out, xor_1_out;

  assign controlled_buffer_1_out = SUB ? {8{1'b1}} : 8'bz;  // Controlled_Buffer controlled_buffer_1
  assign controlled_buffer_1_out = not_1_out ? {8{1'b0}} : 8'bz;  // Controlled_Buffer controlled_buffer_2
  not not_1 (not_1_out, SUB);
  assign xor_1_out = B_IN ^ controlled_buffer_1_out;  // XOR_Gate xor_1, 8 bits wide
  Adder adder_1 (.a(A_IN), .b(xor_1_out), .out(ALWAYS_OUT), .cin(SUB), .cout(COUT));
  assign ALU_DATA_OUT = OUTPUT_ENB ? ALWAYS_OUT : 8'bz;  // Controlled_Buffer controlled_buffer_3
endmodule

module REGISTER_B (
  input  [7:0] DATA_IN,
  input  B_IN,
  input  B_OUT,
  input  CLOCK,
  input  RESET,
  output [7:0] ALWAYS_OUT,
  output [7:0] DATA_OUT
);

  Register register_1 (.D(DATA_IN), .en(B_IN), .clk(CLOCK), .Q(ALWAYS_OUT), .clr(RESET));
  assign DATA_OUT = B_OUT ? ALWAYS_OUT : 8'bz;  // Controlled_Buffer controlled_buffer_1
endmodule

module OUTPUT_REGISTER (
  input  [7:0] DATA_IN,
  input  STORE,
  input  CLOCK,
  input  RESET,
  output [7:0] DATA_OUT
);

  Register register_1 (.D(DATA_IN), .en(STORE), .clk(CLOCK), .Q(DATA_OUT), .clr(RESET));
endmodule

module MAR (
  input  [3:0] DATA_IN,
  input  MAR_IN,
  input  MAR_OUT,
  input  CLOCK,
  input  MAR_RESET,
  output [3:0] ALWAYS_OUT,
  output [3:0] DATA_OUT
);

  Register #(.width(4)) register_1 (.D(DATA_IN), .en(MAR_IN), .clk(CLOCK), .Q(ALWAYS_OUT), .clr(MAR_RESET));
  assign DATA_OUT = MAR_OUT ? ALWAYS_OUT : 4'bz;  // Controlled_Buffer controlled_buffer_1
endmodule

module MEMORY (
  input  [7:0] DATA,
  input  STORE,
  input  CLOCK,
  input  [3:0] ADDRESS,
  input  RAM_OUT_ENB,
  output [7:0] ALWAYS_OUT,
  output [7:0] RAM_OUT
);

  wire and_1_out, and_2_out, and_3_out, and_4_out, and_5_out, and_6_out, and_7_out, and_8_out, and_9_out,
       and_10_out, and_11_out, and_12_out, and_13_out, and_14_out, and_15_out, and_16_out, decoder_1_out0,
       decoder_1_out1, decoder_1_out2, decoder_1_out3, decoder_1_out4, decoder_1_out5, decoder_1_out6,
       decoder_1_out7, decoder_1_out8, decoder_1_out9, decoder_1_out10, decoder_1_out11, decoder_1_out12,
       decoder_1_out13, decoder_1_out14, decoder_1_out15;
  wire [7:0] demultiplexer_1_out0, demultiplexer_1_out1, demultiplexer_1_out2, demultiplexer_1_out3,
       demultiplexer_1_out4, demultiplexer_1_out5, demultiplexer_1_out6, demultiplexer_1_out7,
       demultiplexer_1_out8, demultiplexer_1_out9, demultiplexer_1_out10, demultiplexer_1_out11,
       demultiplexer_1_out12, demultiplexer_1_out13, demultiplexer_1_out14, demultiplexer_1_out15,
       register_1_q, register_2_q, register_3_q, register_4_q, register_5_q, register_6_q, register_7_q,
       register_8_q, register_9_q, register_10_q, register_11_q, register_12_q, register_13_q, register_14_q,
       register_15_q, register_16_q;

  Demultiplexer #(.select(4), .width(8)) demultiplexer_1 (
    .out0(demultiplexer_1_out0), .out1(demultiplexer_1_out1), .out2(demultiplexer_1_out2),
    .out3(demultiplexer_1_out3), .out4(demultiplexer_1_out4), .out5(demultiplexer_1_out5),
    .out6(demultiplexer_1_out6), .out7(demultiplexer_1_out7), .out8(demultiplexer_1_out8),
    .out9(demultiplexer_1_out9), .out10(demultiplexer_1_out10), .out11(demultiplexer_1_out11),
    .out12(demultiplexer_1_out12), .out13(demultiplexer_1_out13), .out14(demultiplexer_1_out14),
    .out15(demultiplexer_1_out15), .in(DATA), .sel(ADDRESS));
  Decoder #(.select(4)) decoder_1 (
    .out0(decoder_1_out0), .out1(decoder_1_out1), .out2(decoder_1_out2), .out3(decoder_1_out3),
    .out4(decoder_1_out4), .out5(decoder_1_out5), .out6(decoder_1_out6), .out7(decoder_1_out7),
    .out8(decoder_1_out8), .out9(decoder_1_out9), .out10(decoder_1_out10), .out11(decoder_1_out11),
    .out12(decoder_1_out12), .out13(decoder_1_out13), .out14(decoder_1_out14), .out15(decoder_1_out15),
    .sel(ADDRESS));  // open: en
  and and_1 (and_1_out, decoder_1_out0, STORE);
  and and_2 (and_2_out, decoder_1_out1, STORE);
  and and_3 (and_3_out, decoder_1_out2, STORE);
  and and_4 (and_4_out, decoder_1_out3, STORE);
  and and_5 (and_5_out, decoder_1_out4, STORE);
  and and_6 (and_6_out, decoder_1_out5, STORE);
  and and_7 (and_7_out, decoder_1_out6, STORE);
  and and_8 (and_8_out, decoder_1_out7, STORE);
  and and_9 (and_9_out, decoder_1_out8, STORE);
  and and_10 (and_10_out, decoder_1_out9, STORE);
  and and_11 (and_11_out, decoder_1_out10, STORE);
  and and_12 (and_12_out, decoder_1_out11, STORE);
  and and_13 (and_13_out, decoder_1_out12, STORE);
  and and_14 (and_14_out, decoder_1_out13, STORE);
  and and_15 (and_15_out, decoder_1_out14, STORE);
  and and_16 (and_16_out, decoder_1_out15, STORE);
  Register register_1 (.D(demultiplexer_1_out0), .en(and_1_out), .clk(CLOCK), .Q(register_1_q));  // open: clr
  Register register_2 (.D(demultiplexer_1_out1), .en(and_2_out), .clk(CLOCK), .Q(register_2_q));  // open: clr
  Register register_3 (.D(demultiplexer_1_out2), .en(and_3_out), .clk(CLOCK), .Q(register_3_q));  // open: clr
  Register register_4 (.D(demultiplexer_1_out3), .en(and_4_out), .clk(CLOCK), .Q(register_4_q));  // open: clr
  Register register_5 (.D(demultiplexer_1_out4), .en(and_5_out), .clk(CLOCK), .Q(register_5_q));  // open: clr
  Register register_6 (.D(demultiplexer_1_out5), .en(and_6_out), .clk(CLOCK), .Q(register_6_q));  // open: clr
  Register register_7 (.D(demultiplexer_1_out6), .en(and_7_out), .clk(CLOCK), .Q(register_7_q));  // open: clr
  Register register_8 (.D(demultiplexer_1_out7), .en(and_8_out), .clk(CLOCK), .Q(register_8_q));  // open: clr
  Register register_9 (.D(demultiplexer_1_out8), .en(and_9_out), .clk(CLOCK), .Q(register_9_q));  // open: clr
  Register register_10 (.D(demultiplexer_1_out9), .en(and_10_out), .clk(CLOCK), .Q(register_10_q));  // open: clr
  Register register_11 (.D(demultiplexer_1_out10), .en(and_11_out), .clk(CLOCK), .Q(register_11_q));  // open: clr
  Register register_12 (.D(demultiplexer_1_out11), .en(and_12_out), .clk(CLOCK), .Q(register_12_q));  // open: clr
  Register register_13 (.D(demultiplexer_1_out12), .en(and_13_out), .clk(CLOCK), .Q(register_13_q));  // open: clr
  Register register_14 (.D(demultiplexer_1_out13), .en(and_14_out), .clk(CLOCK), .Q(register_14_q));  // open: clr
  Register register_15 (.D(demultiplexer_1_out14), .en(and_15_out), .clk(CLOCK), .Q(register_15_q));  // open: clr
  Register register_16 (.D(demultiplexer_1_out15), .en(and_16_out), .clk(CLOCK), .Q(register_16_q));  // open: clr
  Multiplexer #(.select(4), .width(8)) multiplexer_1 (
    .in0(register_1_q), .in1(register_2_q), .in2(register_3_q), .in3(register_4_q), .in4(register_5_q),
    .in5(register_6_q), .in6(register_7_q), .in7(register_8_q), .in8(register_9_q), .in9(register_10_q),
    .in10(register_11_q), .in11(register_12_q), .in12(register_13_q), .in13(register_14_q),
    .in14(register_15_q), .in15(register_16_q), .out(ALWAYS_OUT), .sel(ADDRESS));
  assign RAM_OUT = RAM_OUT_ENB ? ALWAYS_OUT : 8'bz;  // Controlled_Buffer controlled_buffer_1
endmodule

module INSTRUCTION_REGISTER (
  input  [7:0] DATA_IN,
  input  STORE,
  input  DATA_OUT_ENABLE,
  input  RESET,
  input  CLOCK,
  output [7:0] ALWAYS_OUT,
  output [7:0] DATA_OUT
);

  wire [7:4] pull_resistor_1_node;

  Register register_1 (.D(DATA_IN), .en(STORE), .clk(CLOCK), .Q(ALWAYS_OUT), .clr(RESET));
  Pull_Resistor pull_resistor_1 (.node(pull_resistor_1_node[4]));
  Pull_Resistor pull_resistor_2 (.node(pull_resistor_1_node[5]));
  Pull_Resistor pull_resistor_3 (.node(pull_resistor_1_node[6]));
  Pull_Resistor pull_resistor_4 (.node(pull_resistor_1_node[7]));
  assign DATA_OUT = DATA_OUT_ENABLE ? {pull_resistor_1_node, ALWAYS_OUT[3:0]} : 8'bz;  // Controlled_Buffer controlled_buffer_1
endmodule

module STEP_COUNTER (
  input  RESET,
  input  CLOCK,
  output [3:0] BINARY_OUT
);

  Counter #(.max('hf), .width(4)) counter_1 (
    .clr(RESET), .up(1'b1), .count(1'b1), .clk(CLOCK), .Q(BINARY_OUT));  // open: load, D, carry
endmodule

module ZERO_FLAG (
  input  [7:0] in_1,
  output ZERO
);

  wire and_1_out, and_2_out, nor_1_out, nor_2_out, nor_3_out, nor_4_out;

  nor nor_1 (nor_1_out, in_1[0], in_1[1]);
  nor nor_2 (nor_2_out, in_1[2], in_1[3]);
  nor nor_3 (nor_3_out, in_1[4], in_1[5]);
  nor nor_4 (nor_4_out, in_1[6], in_1[7]);
  and and_1 (and_1_out, nor_1_out, nor_2_out);
  and and_2 (and_2_out, nor_3_out, nor_4_out);
  and and_3 (ZERO, and_1_out, and_2_out);
endmodule

module FLAGS (
  input  CARRY,
  input  ZERO,
  input  STORE,
  input  CLOCK,
  input  RESET,
  output CARRY_OUT,
  output ZERO_OUT
);

  Register #(.width(1)) register_1 (.D(CARRY), .en(STORE), .clk(CLOCK), .Q(CARRY_OUT), .clr(RESET));
  Register #(.width(1)) register_2 (.D(ZERO), .en(STORE), .clk(CLOCK), .Q(ZERO_OUT), .clr(RESET));
endmodule
